# Fritzing sketch digram (saved by Fritzing 0.9.3b)
breadboards: 1

parts:
  GY-NEO6MV3 = SUP500F [package=sup500f]
  Part1 = SRF05 Ultrasonic Rangefinder
  M1 = DOIT Esp32 DevKit v1 (30 pins long, 11 pins width) [part_number=ESP32S-PIN30]

nets:
  GND: GY-NEO6MV3.RX-I, GY-NEO6MV3.TX-O, GY-NEO6MV3.GND, Part1.GND, M1.GND, M1.D25, M1.D26
  VCC: GY-NEO6MV3.VCC, Part1.VCC, Part1.Trig, M1.3V3, M1.D13
  N1: Part1.Echo, M1.D12

custom parts:
  DOIT Esp32 DevKit v1 (30 pins long, 11 pins width): The DOIT Esp32 DevKit v1 is one of the development board created by DOIT to evaluate the ESP-WROOM-32 module. It is based on the ESP32 microcontroller that boasts Wifi, Bluetooth, Ethernet and Low Power support all in a single chip. (vanepp) made breadboard work, adjusted pin numbering and labels and reduced size of schematic and cleaned up pcb. This chip is 30pins long (2 x15) and 11 pins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

// code stored in the sketch: main.ino

#include <SoftwareSerial.h>
#include <TinyGPS++.h>

const int trigPin = 12;
const int echoPin = 13;


// define sound speed in cm/uS
#define SOUND_SPEED 0.034
#define CM_TO_INCH 0.393701
int distance; // variable for the distance measurement
long duration;



// gps
TinyGPSPlus gps;
static const int RXPin = 25, TXPin = 26;
int GPSBaud = 9600;
SoftwareSerial gpsSerial(RXPin, TXPin);
// gps
void setup()
{
  // Initialize serial and wait for port to open:
  Serial.begin(9600);
  // Initialize gps Serial:
  gpsSerial.begin(GPSBaud);
  // This delay gives the chance to wait for a Serial Monitor without blocking if none is found
  pinMode(trigPin, OUTPUT); // Sets the trigPin as an Output
  pinMode(echoPin, INPUT);  // Sets the echoPin as an Input


  // Defined in thingProperties.h
  initProperties();


  // Connect to Arduino IoT Cloud
  ArduinoCloud.begin(ArduinoIoTPreferredConnection);
  delay(1500);


  setDebugMessageLevel(2);
  ArduinoCloud.printDebugInfo();
}


void loop()
{
  ArduinoCloud.update();
  
  int ultrasonicl = ultrasonic();
   Serial.print("ultrasonicl : ");
   Serial.println(ultrasonicl);


  pinultrasonic = ultrasonicl;


  if (ultrasonicl > 30)
  {
    // put information in arduino iot cloud
    stauteultra = "full"; 
    loaded = true;
  }
  else
  {
    // put information in arduino iot cloud to tel me about 
    stauteultra = "not full";
    loaded = false;
  }


  // if gpsSerial is available and bigar then 0
  while (gpsSerial.available() > 0)
  {
    // will check and encode from gpsSerial and read
    if (gps.encode(gpsSerial.read()))
    {
      float latitude = gps.location.lat();
      float longitude = gps.location.lng();
      //boardGPS = Location(latitude, longitude);


      // watch the gps location length
       Serial.print("Latitude: ");
       Serial.println(gps.location.lat(), 6);
       Serial.print("Longitude: ");
       Serial.println(gps.location.lng(), 6);
       Serial.print("Altitude: ");
       Serial.println(gps.altitude.meters());
    }
  }


  delay(100);
}


int ultrasonic()
{
  digitalWrite(trigPin, LOW);
  delayMicroseconds(2);
  // Sets the trigPin HIGH (ACTIVE) for 10 microseconds
  digitalWrite(trigPin, HIGH);
  delayMicroseconds(10);
  digitalWrite(trigPin, LOW);
  // Reads the echoPin, returns the sound wave travel time in microseconds
  duration = pulseIn(echoPin, HIGH);
  // Calculating the distance
  distance = duration * 0.034 / 2; // Speed of sound wave divided by 2 (go and back)
  // Serial.println(distance);
  return distance;
}



void onUltrasonicChange(){}
void onSwitchultraChange(){}
void onStauteultraChange(){}
void onPinultrasonicChange(){}
void onBoardGPSChange(){}
void onLoadedChange(){}
